# Fritzing sketch mp3alarm_pcb (saved by Fritzing 0.9.3b)
circuit board: 7cm x 4.5cm
breadboards: 1

parts:
  ESP32_Mini = MH-ET Live Minikit for ESP32
  UDA1334 = Adafruit UDA1334 I2S DAC [part_number="Adafruit #3678"]
  U3 = microSD Socket [package=usd-socket-pp]
  J1 = female pin header, 2 pins [form="♀ (female)"]
  J2 = female pin header, 2 pins [form="♀ (female)"]
  J3 = female pin header, 2 pins [form="♀ (female)"]
  R_G_L = female pin header, 3 pins [form="♀ (female)"]
  SCL_SDA_GND_5V = female pin header, 4 pins [form="♀ (female)"]
  5V_D_GND = female pin header, 3 pins [form="♀ (female)"]

nets:
  GND: ESP32_Mini.GND, UDA1334.GND, UDA1334.AGND, U3.SHIELD, U3.GND, J1.pin1, J2.pin1, J3.pin1, R_G_L.pin2, SCL_SDA_GND_5V.pin3, 5V_D_GND.pin3
  N1: ESP32_Mini.IO35, J3.pin2
  N2: ESP32_Mini.IO33, J1.pin2
  N3: ESP32_Mini.IO34, J2.pin2
  N4: ESP32_Mini.IO26, 5V_D_GND.pin2
  N5: ESP32_Mini.IO18, U3.SCK
  N6: ESP32_Mini.IO19, U3.DO
  N7: ESP32_Mini.IO23, U3.DI
  N8: ESP32_Mini.IO5, U3.CS
  3.3V: ESP32_Mini.3.3V, U3.VCC
  N9: ESP32_Mini.IO22, SCL_SDA_GND_5V.pin1
  N10: ESP32_Mini.IO21, SCL_SDA_GND_5V.pin2
  VCC: ESP32_Mini.VCC, UDA1334.VIN, SCL_SDA_GND_5V.pin4, 5V_D_GND.pin1
  N11: ESP32_Mini.IO27, UDA1334.WORDSEL_IN
  N12: ESP32_Mini.IO25, UDA1334.DATA_IN
  N13: ESP32_Mini.IO4, UDA1334.BITCLK_IN
  N14: UDA1334.OUTL, R_G_L.pin3
  N15: UDA1334.OUTR, R_G_L.pin1

custom parts:
  MH-ET Live Minikit for ESP32: MH-ET Live Minikit for ESP32 ( http://mh.nodebb.com/topic/8/mh-et-live-minikit-for-esp32/2/) PCB footprint is invalid.
  Adafruit UDA1334 I2S DAC: This fully-featured UDA1334A I2S Stereo DAC breakout is a perfect match for any I2S-output audio interface. It's affordable but sounds great! The NXP UDA1334A is a jack-of-all-I2S-trades: you can use 3.3V - 5V logic levels (a rarity), and can process multiple different formats by setting two pins to high or low. The DAC will process data immediately, and give you a clear, analog, stereo line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
