# Fritzing sketch pcb (saved by Fritzing 0.9.3b)
circuit board: 7cm x 4.5cm
breadboards: 1

parts:
  MH-ET_Live_Minikit_for_ESP1 = MH-ET Live Minikit for ESP32
  Bauteil1 = Adafruit UDA1334 I2S DAC [part_number="Adafruit #3678"]
  U3 = microSD Socket [package=usd-socket-pp]
  J1 = female pin header, 2 pins [form="♀ (female)"]
  J2 = female pin header, 2 pins [form="♀ (female)"]
  J3 = female pin header, 2 pins [form="♀ (female)"]
  J4 = female pin header, 3 pins [form="♀ (female)"]
  J5 = female pin header, 4 pins [form="♀ (female)"]

nets:
  GND: MH-ET_Live_Minikit_for_ESP1.GND, Bauteil1.GND, Bauteil1.AGND, U3.SHIELD, U3.GND, J1.pin1, J2.pin1, J3.pin1, J4.pin2, J5.pin3
  N1: MH-ET_Live_Minikit_for_ESP1.IO35, J3.pin2
  N2: MH-ET_Live_Minikit_for_ESP1.IO33, J1.pin2
  N3: MH-ET_Live_Minikit_for_ESP1.IO34, J2.pin2
  N4: MH-ET_Live_Minikit_for_ESP1.IO18, U3.SCK
  N5: MH-ET_Live_Minikit_for_ESP1.IO19, U3.DO
  N6: MH-ET_Live_Minikit_for_ESP1.IO23, U3.DI
  N7: MH-ET_Live_Minikit_for_ESP1.IO5, U3.CS
  3.3V: MH-ET_Live_Minikit_for_ESP1.3.3V, U3.VCC
  N8: MH-ET_Live_Minikit_for_ESP1.IO22, J5.pin1
  N9: MH-ET_Live_Minikit_for_ESP1.IO21, J5.pin2
  VCC: MH-ET_Live_Minikit_for_ESP1.VCC, Bauteil1.VIN, J5.pin4
  N10: MH-ET_Live_Minikit_for_ESP1.IO27, Bauteil1.WORDSEL_IN
  N11: MH-ET_Live_Minikit_for_ESP1.IO25, Bauteil1.DATA_IN
  N12: MH-ET_Live_Minikit_for_ESP1.IO4, Bauteil1.BITCLK_IN
  N13: Bauteil1.OUTL, J4.pin3
  N14: Bauteil1.OUTR, J4.pin1

custom parts:
  MH-ET Live Minikit for ESP32: MH-ET Live Minikit for ESP32 ( http://mh.nodebb.com/topic/8/mh-et-live-minikit-for-esp32/2/) PCB footprint is invalid.
  Adafruit UDA1334 I2S DAC: This fully-featured UDA1334A I2S Stereo DAC breakout is a perfect match for any I2S-output audio interface. It's affordable but sounds great! The NXP UDA1334A is a jack-of-all-I2S-trades: you can use 3.3V - 5V logic levels (a rarity), and can process multiple different formats by setting two pins to high or low. The DAC will process data immediately, and give you a clear, analog, stereo line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
